# Fritzing sketch LightClock (saved by Fritzing 0.8.7b)
breadboards: 1

parts:
  Part1 = Arduino Uno (Rev3)
  neopixel1 = Neopixel Ring 12
  neopixel2 = Neopixel 24 Ring
  R1 = Resistor [tolerance=±5% resistance=330 package=THT]
  R2 = Resistor [tolerance=±5% resistance=330 package=THT]
  R3 = Resistor [tolerance=±5% resistance=330 package=THT]
  JACK1 = 2.1mm Barrel Jack with Terminal Block
  C1 = Electrolytic Capacitor [capacitance=1mF voltage=35V package="300 mil [THT, electrolytic]"]

nets:
  N1: Part1.D4, R2.Pin_0
  N2: Part1.D5_PWM, R3.Pin_0
  N3: Part1.D6_PWM, R1.Pin_0
  GND: neopixel1.GND, neopixel2.GND, JACK1.NEG, C1.-
  VCC: neopixel1.VCC, neopixel2.Vcc, JACK1.POS, C1.+
  N4: neopixel1.IN, R1.Pin_1
  N5: neopixel2.IN, R2.Pin_1

notes:
  5V
  GND
  SDA
  SCL
  ChronoDot
  NeoPixel 60 LEDs Ring

custom parts:
  Neopixel Ring 12: Neopixel Ring x12
